// Logisim project Circuito Tarea 3.circ as structural Verilog: 2 circuits, main circuit main
module main (
  input  in_1,
  input  in_2,
  input  in_3
);

  wire and_1_out, and_2_out, and_3_out, and_4_out, and_5_out, button_1_out, clock_1_out, not_1_out,
       not_2_out, not_3_out, or_1_out, or_2_out;

  not not_1 (not_1_out, in_2);
  not not_2 (not_2_out, in_1);
  not not_3 (not_3_out, in_3);
  and and_1 (and_1_out, in_1, not_3_out);
  and and_2 (and_2_out, in_1, not_1_out);
  and and_3 (and_3_out, not_2_out, in_2, in_3);
  and and_4 (and_4_out, in_2, not_3_out);
  and and_5 (and_5_out, not_1_out, in_3);
  Button button_1 (.out(button_1_out));
  or or_1 (or_1_out, and_1_out, and_2_out, and_3_out);
  or or_2 (or_2_out, and_4_out, and_5_out);
  Clock clock_1 (.out(clock_1_out));
  D_Flip_Flop d_ff_1 (.clk(clock_1_out), .D(or_1_out), .Q(in_1), .reset(button_1_out));  // open: Qn, preset, en
  D_Flip_Flop d_ff_2 (.clk(clock_1_out), .D(or_2_out), .Q(in_2), .reset(button_1_out));  // open: Qn, preset, en
  D_Flip_Flop d_ff_3 (.clk(clock_1_out), .D(not_3_out), .Q(in_3), .reset(button_1_out));  // open: Qn, preset, en
endmodule

module caja (
  input  in_1,
  input  in_2,
  input  in_3
);

  // AND_Gate and_1 is placed but not wired
  // AND_Gate and_2 is placed but not wired
  // OR_Gate or_1 is placed but not wired
endmodule
