// Logisim project Ejercicio1.1.circ as structural Verilog
module _1 (
);

  wire A_out, and_1_out, and_2_out, and_3_out, B_out, C_out, D_out, not_1_out, not_2_out, not_3_out,
       not_4_out, not_5_out, not_6_out, or_1_out, or_2_out;

  Button A (.out(A_out));
  Button B (.out(B_out));
  Button C (.out(C_out));
  Button D (.out(D_out));
  not not_1 (not_1_out, A_out);
  not not_2 (not_2_out, B_out);
  not not_3 (not_3_out, C_out);
  and and_1 (and_1_out, not_3_out, not_4_out);
  not not_4 (not_4_out, D_out);
  not not_5 (not_5_out, C_out);
  and and_2 (and_2_out, not_5_out, D_out);
  and and_3 (and_3_out, C_out, not_6_out);
  not not_6 (not_6_out, D_out);
  or or_1 (or_1_out, not_2_out, and_1_out);
  or or_2 (or_2_out, and_2_out, and_3_out);
  LED Y1 (.in(not_1_out));
  LED Y2 (.in(or_1_out));
  LED Y3 (.in(or_2_out));
  LED Y4 (.in(D_out));
endmodule
