// Logisim project Ejercicio2.2.circ as structural Verilog: 2 circuits, main circuit main
module main (
);

  wire A1_out, A2_out, A3_out, A4_out, A5_out, A6_out, A7_out, A8_out, A9_out, A10_out, A11_out, A12_out,
       A13_out, A14_out, A15_out, A16_out, CarryIn_out, suma_1_co, suma_2_co, suma_3_co, suma_4_co,
       suma_5_co, suma_6_co, suma_7_co, suma_8_co, suma_9_co, suma_10_co, suma_11_co, suma_12_co, suma_13_co,
       suma_14_co, suma_15_co, suma_16_co, undriven;

  Button CarryIn (.out(CarryIn_out));
  Button A2 (.out(A2_out));
  Button A1 (.out(A1_out));
  suma suma_1 (.Co(suma_1_co));
  LED led_1 (.in(suma_1_co));
  Button A3 (.out(A3_out));
  suma suma_2 (.Co(suma_2_co));
  LED led_2 (.in(suma_2_co));
  Button A4 (.out(A4_out));
  suma suma_3 (.Co(suma_3_co));
  suma suma_4 (.Co(suma_4_co));
  LED led_3 (.in(suma_3_co));
  LED led_4 (.in(suma_4_co));
  Button A6 (.out(A6_out));
  Button A5 (.out(A5_out));
  suma suma_5 (.Co(suma_5_co));
  LED led_5 (.in(suma_5_co));
  Button A7 (.out(A7_out));
  suma suma_6 (.Co(suma_6_co));
  LED led_6 (.in(suma_6_co));
  Button A8 (.out(A8_out));
  suma suma_7 (.Co(suma_7_co));
  suma suma_8 (.Co(suma_8_co));
  LED led_7 (.in(suma_8_co));
  Button A10 (.out(A10_out));
  Button A9 (.out(A9_out));
  suma suma_9 (.Co(suma_9_co));
  LED led_8 (.in(suma_7_co));
  LED led_9 (.in(suma_9_co));
  Button A11 (.out(A11_out));
  suma suma_10 (.Co(suma_10_co));
  LED led_10 (.in(suma_10_co));
  Button A12 (.out(A12_out));
  suma suma_11 (.Co(suma_11_co));
  suma suma_12 (.Co(suma_12_co));
  LED led_11 (.in(suma_12_co));
  Button A14 (.out(A14_out));
  Button A13 (.out(A13_out));
  suma suma_13 (.Co(suma_13_co));
  LED led_12 (.in(suma_11_co));
  LED led_13 (.in(suma_13_co));
  Button A15 (.out(A15_out));
  suma suma_14 (.Co(suma_14_co));
  LED led_14 (.in(suma_14_co));
  Button A16 (.out(A16_out));
  suma suma_15 (.Co(suma_15_co));
  suma suma_16 (.Co(suma_16_co));
  LED led_15 (.in(suma_16_co));
  LED CarryOut (.in(undriven));
  LED led_16 (.in(suma_15_co));

  // Notes on the sheet:
  //   COMPLEMENTO A2 [16 BITS]
endmodule

module suma (
  output Co
);

  wire A_out, and_2_out, and_3_out, Ci_out, not_1_out, not_2_out, not_3_out, or_1_out;

  Button A (.out(A_out));
  not not_1 (not_1_out, A_out);
  Button Ci (.out(Ci_out));
  not not_2 (not_2_out, not_1_out);
  not not_3 (not_3_out, Ci_out);
  and and_1 (Co, not_1_out, Ci_out);
  and and_2 (and_2_out, not_2_out, Ci_out);
  and and_3 (and_3_out, not_1_out, not_3_out);
  LED B (.in(or_1_out));
  or or_1 (or_1_out, and_2_out, and_3_out);
endmodule
